# Fritzing sketch sketch (saved by Fritzing 0.9.4)
breadboards: 1

parts:
  Part1 = Adafruit Feather HUZZAH ESP8266 [part_number="Adafruit #2821"]
  LCD1 = LCD screen
  LCM1602_IIC1 = LCM1602 IIC [part_number="LCM1602 IIC" chip_label="LCM1602 IIC" package="DIP (Dual Inline) [THT]"]
  LED1 = LED - 3mm [color="Red (633nm)" package="3 mm [THT]"]
  R1 = Resistor [tolerance=±5% resistance=220 package="1206 [SMD]"]

nets:
  N1: Part1.RXD, LED1.anode
  GND: Part1.GND, LCM1602_IIC1.GND, R1.Pin_1
  N2: Part1.VBUS, LCM1602_IIC1.VCC
  N3: Part1.GPIO5/SCL, LCM1602_IIC1.SDA
  N4: Part1.GPIO4/SDA, LCM1602_IIC1.SCL
  VSS: LCD1.VSS, LCM1602_IIC1.VSS
  VDD: LCD1.VDD, LCM1602_IIC1.VDD
  N5: LCD1.V0, LCM1602_IIC1.V0
  N6: LCD1.RS, LCM1602_IIC1.RS
  N7: LCD1.R/W, LCM1602_IIC1.RW
  N8: LCD1.E, LCM1602_IIC1.E
  N9: LCD1.DB0, LCM1602_IIC1.D0
  N10: LCD1.DB1, LCM1602_IIC1.D1
  N11: LCD1.DB2, LCM1602_IIC1.D2
  N12: LCD1.DB3, LCM1602_IIC1.D3
  N13: LCD1.DB4, LCM1602_IIC1.D4
  N14: LCD1.DB5, LCM1602_IIC1.D5
  N15: LCD1.DB6, LCM1602_IIC1.D6
  N16: LCD1.DB7, LCM1602_IIC1.D7
  N17: LCD1.LED+, LCM1602_IIC1.A
  N18: LCD1.LED-, LCM1602_IIC1.K
  N19: LCM1602_IIC1.LED_A, LCM1602_IIC1.LED_B
  N20: LED1.cathode, R1.Pin_0

custom parts:
  Adafruit Feather HUZZAH ESP8266: his is the Adafruit Feather HUZZAH ESP8266 - our take on an 'all-in-one' ESP8266 WiFi development board with built in USB and battery charging. Its an ESP8266 WiFi module with all the extras you need, ready to rock! We have other boards in the Feather family, check'em out here. At the Feather HUZZAH's heart is an ESP8266 WiFi microcontroller clocked at 80 MHz and at 3.3V logic. This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
  LCM1602 IIC: I2C-Module to use a 1602 or 2004 LCD on with the wire.h libory Serial LCD Modul
